// Logisim project Exemplo_0601.circ as structural Verilog: 2 circuits, main circuit main
module main (
  input  A,
  input  B,
  output S,
  output S_2
);

  and AND (S, A, B);
  or OR (S_2, A, B);
endmodule

// main
module LU_0601 (
  input  A,
  input  B,
  output out_3,
  output out_4
);

  main LU (.A(A), .B(B), .S(out_3), .S_2(out_4));
endmodule
