// Logisim project Exemplo_0602.circ as structural Verilog: 2 circuits, main circuit main
module main (
  input  A,
  input  B,
  input  in_3,
  output out_4
);

  wire and_1_out, or_1_out;

  and and_1 (and_1_out, A, B);
  or or_1 (or_1_out, A, B);
  Multiplexer #(.enable("false")) multiplexer_1 (.in0(and_1_out), .in1(or_1_out), .out(out_4), .sel(in_3));
endmodule

// main
module LU_0602 (
  input  A,
  input  B,
  input  S,
  output out_4
);

  main LU (.A(A), .B(B), .in_3(S), .out_4(out_4));
endmodule
