// Logisim project Exemplo_0603.circ as structural Verilog: 1 circuit, main circuit main
module main (
  input  a,
  input  b,
  input  c,
  output x,
  output y
);

  wire and_1_out, and_2_out, and_3_out, and_4_out, and_5_out, and_6_out, and_7_out, nand_1_out, nor_1_out,
       not_1_out, not_2_out, or_1_out, or_2_out;

  not not_1 (not_1_out, a);
  or or_1 (or_1_out, b, c);
  or or_2 (or_2_out, b, c);
  and and_1 (and_1_out, b, b);
  and and_2 (and_2_out, c, not_1_out);
  and and_3 (and_3_out, or_1_out, or_2_out);
  not not_2 (not_2_out, a);
  nand nand_1 (nand_1_out, b, c);
  and and_4 (and_4_out, nand_1_out, a);
  nor nor_1 (nor_1_out, b, c);
  and and_5 (and_5_out, nor_1_out, a);
  and and_6 (and_6_out, and_1_out, and_2_out);
  and and_7 (and_7_out, and_3_out, not_2_out);
  or or_3 (y, and_4_out, and_5_out);
  or or_4 (x, and_6_out, and_7_out);
endmodule
