// Logisim project Exemplo_0604.circ as structural Verilog: 1 circuit, main circuit main
module main (
  input  a,
  input  b,
  input  c,
  input  d,
  output s
);

  wire and_1_out, and_2_out, and_3_out, and_4_out, and_5_out, and_6_out, and_7_out, and_8_out, nor_1_out,
       not_1_out, not_2_out, not_3_out, not_4_out, or_1_out, or_2_out, or_3_out, or_4_out, xnor_1_out,
       xor_1_out;

  or or_1 (or_1_out, c, d);
  xor xor_1 (xor_1_out, c, d);
  xnor xnor_1 (xnor_1_out, c, d);
  not not_1 (not_1_out, a);
  or or_2 (or_2_out, c, d);
  not not_2 (not_2_out, a);
  nor nor_1 (nor_1_out, or_1_out, d);
  and and_1 (and_1_out, a, xor_1_out);
  and and_2 (and_2_out, and_1_out, not_3_out);
  not not_3 (not_3_out, b);
  and and_3 (and_3_out, a, xnor_1_out);
  and and_4 (and_4_out, and_3_out, b);
  and and_5 (and_5_out, not_1_out, or_2_out);
  and and_6 (and_6_out, and_5_out, not_4_out);
  not not_4 (not_4_out, b);
  and and_7 (and_7_out, not_2_out, nor_1_out);
  and and_8 (and_8_out, and_7_out, b);
  or or_3 (or_3_out, and_2_out, and_4_out);
  or or_4 (or_4_out, and_6_out, and_8_out);
  or or_5 (s, or_3_out, or_4_out);
endmodule
