// Logisim project Exemplo_0605.circ as structural Verilog: 1 circuit, main circuit main
module main (
  input  a,
  input  b,
  input  c,
  input  d,
  input  e,
  output x
);

  wire and_1_out, and_2_out, and_3_out, and_4_out, and_5_out, and_6_out, and_7_out, and_8_out, and_9_out,
       and_10_out, and_11_out, and_12_out, and_13_out, and_14_out, and_15_out, and_16_out, and_17_out,
       and_18_out, and_19_out, and_20_out, and_21_out, and_22_out, and_23_out, and_24_out, and_25_out,
       nand_1_out, nor_1_out, not_1_out, not_2_out, not_3_out, not_4_out, not_5_out, not_6_out, not_7_out,
       not_8_out, not_9_out, not_10_out, not_11_out, not_12_out, not_13_out, not_14_out, or_1_out, or_2_out,
       or_3_out, or_4_out, or_5_out, or_6_out, or_7_out, xnor_1_out, xor_1_out;

  not not_1 (not_1_out, b);
  not not_2 (not_2_out, a);
  not not_3 (not_3_out, b);
  not not_4 (not_4_out, d);
  not not_5 (not_5_out, c);
  not not_6 (not_6_out, a);
  not not_7 (not_7_out, b);
  not not_8 (not_8_out, e);
  not not_9 (not_9_out, a);
  or or_1 (or_1_out, d, e);
  not not_10 (not_10_out, c);
  not not_11 (not_11_out, a);
  nor nor_1 (nor_1_out, d, e);
  and and_1 (and_1_out, a, not_1_out);
  not not_12 (not_12_out, c);
  not not_13 (not_13_out, b);
  nand nand_1 (nand_1_out, d, e);
  xor xor_1 (xor_1_out, d, e);
  not not_14 (not_14_out, c);
  xnor xnor_1 (xnor_1_out, d, e);
  and and_2 (and_2_out, not_2_out, not_3_out);
  and and_3 (and_3_out, and_2_out, and_4_out);
  and and_4 (and_4_out, not_4_out, not_5_out);
  and and_5 (and_5_out, not_6_out, not_7_out);
  and and_6 (and_6_out, and_5_out, and_7_out);
  and and_7 (and_7_out, not_8_out, c);
  and and_8 (and_8_out, not_9_out, b);
  and and_9 (and_9_out, and_8_out, and_10_out);
  and and_10 (and_10_out, or_1_out, not_10_out);
  and and_11 (and_11_out, not_11_out, b);
  and and_12 (and_12_out, and_11_out, and_13_out);
  and and_13 (and_13_out, nor_1_out, c);
  and and_14 (and_14_out, and_1_out, d);
  and and_15 (and_15_out, and_14_out, and_16_out);
  and and_16 (and_16_out, e, not_12_out);
  and and_17 (and_17_out, a, not_13_out);
  and and_18 (and_18_out, and_17_out, and_19_out);
  and and_19 (and_19_out, nand_1_out, c);
  and and_20 (and_20_out, a, b);
  and and_21 (and_21_out, and_20_out, and_22_out);
  and and_22 (and_22_out, xor_1_out, not_14_out);
  and and_23 (and_23_out, a, b);
  and and_24 (and_24_out, and_23_out, and_25_out);
  and and_25 (and_25_out, xnor_1_out, c);
  or or_2 (or_2_out, and_3_out, and_6_out);
  or or_3 (or_3_out, and_9_out, and_12_out);
  or or_4 (or_4_out, and_15_out, and_18_out);
  or or_5 (or_5_out, and_21_out, and_24_out);
  or or_6 (or_6_out, or_2_out, or_3_out);
  or or_7 (or_7_out, or_4_out, or_5_out);
  or or_8 (x, or_6_out, or_7_out);
endmodule
