// Logisim project Circuito06.circ as structural Verilog: 1 circuit, main circuit main
module main (
  input  A,
  input  B,
  output out_3
);

  wire C_out, D_out, nA_out, nB_out;

  // NOR_Gate nA has open pins: out=nA_out
  // NOR_Gate nB has open pins: out=nB_out
  // NOR_Gate C has open pins: out=C_out
  // NOR_Gate D has open pins: out=D_out
  // NOR_Gate S has open pins: out=out_3
endmodule
